# Fritzing sketch aaa-sq (saved by Fritzing 0.9.2b)
circuit board: 3.21499cm x 2cm
breadboards: 1

parts:
  TRS1 = Audio Jack (TRS) 3.5mm [package="4Ucon 08780 [THT]"]
  C1 = Ceramic Capacitor [capacitance=100nF package="100 mil [THT, multilayer]"]
  C2 = Ceramic Capacitor [capacitance=100nF package="100 mil [THT, multilayer]"]
  R1 = Resistor [tolerance=±5% resistance=5k package=THT]
  R2 = Resistor [tolerance=±5% resistance=100k package=THT]
  R3 = Resistor [tolerance=±5% resistance=5k package=THT]
  R4 = Resistor [tolerance=±5% resistance=5k package=THT]
  R5 = Resistor [tolerance=±5% resistance=100k package=THT]
  J1 = female pin header, 3 pins [form="♀ (female)"]
  J2 = female pin header, 4 pins [form="♀ (female)"]

nets:
  N1: TRS1.Sleeve, R5.Pin_0, J1.pin1, J2.pin4
  N2: TRS1.Ring, C1.0, J1.pin3
  N3: TRS1.Tip, C2.0, J1.pin2
  N4: C1.1, R3.Pin_0
  N5: C2.1, R4.Pin_0
  N6: R1.Pin_0, R2.Pin_0, J2.pin1
  N7: R1.Pin_1, J2.pin2
  N8: R2.Pin_1, R3.Pin_1, R4.Pin_1, R5.Pin_1, J2.pin3

notes:
  GND
  L
  R
  AREF
  3V
  A0
  KreativeKorp
  Arduino Audio Adapter
