# Fritzing sketch BusyBoardMega (saved by Fritzing 0.9.2b)
circuit board: 9.92473cm x 6.87959cm
breadboards: 1

parts:
  J1 = female pin header, 10 pins [form="♀ (female)"]
  J2 = female pin header, 8 pins [form="♀ (female)"]
  J3 = female pin header, 8 pins [form="♀ (female)"]
  J4 = female pin header, 8 pins [form="♀ (female)"]
  J5 = female pin header, 8 pins [form="♀ (female)"]
  J6 = female pin header, 8 pins [form="♀ (female)"]
  J7 = double row female pin header, 36 pins [form="♀ (female)"]  # not connected
  J8 = double row female pin header, 6 pins [form="♀ (female)"]  # not connected
  J9 = double row female pin header, 6 pins [form="♀ (female)"]  # not connected
  J10 = female pin header, 5 pins [form="♀ (female)"]
  J11 = female pin header, 18 pins [form="♀ (female)"]
  J12 = female pin header, 8 pins [form="♀ (female)"]
  J13 = female pin header, 8 pins [form="♀ (female)"]
  J14 = female pin header, 10 pins [form="♀ (female)"]
  J15 = female pin header, 8 pins [form="♀ (female)"]
  J16 = female pin header, 8 pins [form="♀ (female)"]
  J17 = female pin header, 8 pins [form="♀ (female)"]
  TRS2 = Audio Jack (TRS) 3.5mm [package="4Ucon 08780 [THT]"]
  C3 = Ceramic Capacitor [capacitance=100nF package="100 mil [THT, multilayer]"]
  C4 = Ceramic Capacitor [capacitance=100nF package="100 mil [THT, multilayer]"]
  R6 = Resistor [tolerance=±5% resistance=5k package=THT]
  R7 = Resistor [tolerance=±5% resistance=100k package=THT]
  R8 = Resistor [tolerance=±5% resistance=5k package=THT]
  R9 = Resistor [tolerance=±5% resistance=5k package=THT]
  R10 = Resistor [tolerance=±5% resistance=100k package=THT]
  J19 = female pin header, 4 pins [form="♀ (female)"]
  S1 = Pushbutton [package="[THT]"]
  Piezo = female pin header, 2 pins [form="♀ (female)"]
  RPIEZO = Resistor [tolerance=±5% resistance=220 package=THT]
  VS = female pin header, 2 pins [form="♀ (female)"]
  J22 = female pin header, 3 pins [form="♀ (female)"]
  J23 = female pin header, 3 pins [form="♀ (female)"]
  J20 = female pin header, 6 pins [form="♀ (female)"]
  S2 = Pushbutton [package="[THT]"]
  S3 = Pushbutton [package="[THT]"]
  S4 = Pushbutton [package="[THT]"]

nets:
  N1: J1.pin1, J14.pin1
  N2: J1.pin2, J14.pin2
  N3: J1.pin3, J14.pin3, R6.Pin_0, R7.Pin_0, J19.pin1
  N4: J1.pin4, J4.pin6, J4.pin7, J10.pin4, J11.pin1, J14.pin4, J16.pin6, J16.pin7, TRS2.Sleeve, R10.Pin_0, J19.pin4, S1.Pin_3, S1.Pin_4, Piezo.pin1, VS.pin1, J22.pin2, J23.pin2, J20.pin2, S2.Pin_1, S2.Pin_2, S3.Pin_1, S3.Pin_2, S4.Pin_1, S4.Pin_2
  N5: J1.pin5, J14.pin5
  N6: J1.pin6, J14.pin6
  N7: J1.pin7, J14.pin7
  N8: J1.pin8, J14.pin8
  N9: J1.pin9, J14.pin9
  N10: J1.pin10, J14.pin10, RPIEZO.Pin_1
  N11: J2.pin1, J13.pin1
  N12: J2.pin2, J13.pin2, J22.pin1
  N13: J2.pin3, J13.pin3
  N14: J2.pin4, J13.pin4, VS.pin2
  N15: J2.pin5, J13.pin5
  N16: J2.pin6, J13.pin6
  N17: J2.pin7, J13.pin7
  N18: J2.pin8, J13.pin8
  N19: J3.pin1, J12.pin1
  N20: J3.pin2, J11.pin2, J12.pin2
  N21: J3.pin3, J11.pin3, J12.pin3
  N22: J3.pin4, J11.pin4, J12.pin4
  N23: J3.pin5, J11.pin5, J12.pin5
  N24: J3.pin6, J11.pin6, J12.pin6
  N25: J3.pin7, J10.pin1, J12.pin7
  N26: J3.pin8, J10.pin2, J12.pin8
  N27: J4.pin1, J16.pin1
  N28: J4.pin2, J16.pin2
  N29: J4.pin3, J16.pin3, S1.Pin_1, S1.Pin_2
  N30: J4.pin4, J16.pin4, R6.Pin_1, J19.pin2
  N31: J4.pin5, J10.pin5, J16.pin5, J22.pin3, J23.pin3, J20.pin6
  N32: J4.pin8, J16.pin8
  N33: J5.pin1, J15.pin1, R7.Pin_1, R8.Pin_1, R9.Pin_1, R10.Pin_1, J19.pin3
  N34: J5.pin2, J15.pin2, S3.Pin_3, S3.Pin_4
  N35: J5.pin3, J15.pin3, S2.Pin_3, S2.Pin_4
  N36: J5.pin4, J15.pin4, S4.Pin_3, S4.Pin_4
  N37: J5.pin5, J11.pin7, J15.pin5
  N38: J5.pin6, J11.pin8, J15.pin6
  N39: J5.pin7, J11.pin9, J15.pin7
  N40: J5.pin8, J11.pin10, J15.pin8
  N41: J6.pin1, J11.pin11, J17.pin1
  N42: J6.pin2, J11.pin12, J17.pin2
  N43: J6.pin3, J11.pin13, J17.pin3
  N44: J6.pin4, J11.pin14, J17.pin4
  N45: J6.pin5, J11.pin15, J17.pin5
  N46: J6.pin6, J11.pin16, J17.pin6
  N47: J6.pin7, J11.pin17, J17.pin7
  N48: J6.pin8, J11.pin18, J17.pin8
  N49: J10.pin3, J20.pin1
  N50: TRS2.Ring, C3.0, J20.pin3
  N51: TRS2.Tip, C4.0, J20.pin4
  N52: C3.1, R8.Pin_0
  N53: C4.1, R9.Pin_0
  N54: Piezo.pin2, RPIEZO.Pin_0
  N55: J23.pin1, J20.pin5

notes:
  SDA
  SCL
  SQW
  GND
  5V
  RTC
  AREF
  13
  12
  11
  10
  9
  8
  7
  6
  5
  4
  3
  2
  TX-1
  RX-0
  TX3-14
  RX3-15
  RX2-17
  TX2-16
  TX1-18
  RX1-19
  SDA-20
  SCL-21
  IOREF
  RESET
  3.3V
  Vin
  A0
  A1
  A2
  A3
  A4
  A5
  A6
  A7
  A8
  A9
  A10
  A11
  A12
  A13
  A14
  A15
  3V
  R
  L
  Audio Input
  Keyboard
  NeoPixel
  G
  In
  O
  NPO
  Matrix
  A
  B
  C
  BusyBoard Mega by KreativeKorp
