# Fritzing sketch SegTermPanel (saved by Fritzing 0.9.2b)
circuit board: 34cm x 34cm
breadboards: 1

parts:
  J1 = female pin header, 4 pins [form="♀ (female)"]
  J2 = female pin header, 4 pins [form="♀ (female)"]
  J3 = female pin header, 4 pins [form="♀ (female)"]
  J4 = female pin header, 4 pins [form="♀ (female)"]
  J5 = female pin header, 4 pins [form="♀ (female)"]
  J6 = female pin header, 4 pins [form="♀ (female)"]
  J7 = female pin header, 4 pins [form="♀ (female)"]
  J8 = female pin header, 4 pins [form="♀ (female)"]
  J9 = female pin header, 4 pins [form="♀ (female)"]
  J10 = female pin header, 4 pins [form="♀ (female)"]
  J11 = female pin header, 4 pins [form="♀ (female)"]
  J12 = female pin header, 4 pins [form="♀ (female)"]
  J13 = female pin header, 4 pins [form="♀ (female)"]
  J14 = female pin header, 4 pins [form="♀ (female)"]
  J15 = female pin header, 4 pins [form="♀ (female)"]
  J16 = female pin header, 4 pins [form="♀ (female)"]
  J17 = female pin header, 4 pins [form="♀ (female)"]
  J18 = female pin header, 4 pins [form="♀ (female)"]
  J19 = female pin header, 4 pins [form="♀ (female)"]
  J20 = female pin header, 4 pins [form="♀ (female)"]
  J21 = female pin header, 4 pins [form="♀ (female)"]
  J22 = female pin header, 4 pins [form="♀ (female)"]
  J23 = female pin header, 4 pins [form="♀ (female)"]
  J24 = female pin header, 4 pins [form="♀ (female)"]
  J25 = female pin header, 4 pins [form="♀ (female)"]
  J26 = female pin header, 4 pins [form="♀ (female)"]
  J27 = female pin header, 4 pins [form="♀ (female)"]
  J28 = female pin header, 4 pins [form="♀ (female)"]
  J29 = female pin header, 4 pins [form="♀ (female)"]
  J30 = female pin header, 4 pins [form="♀ (female)"]
  J31 = female pin header, 4 pins [form="♀ (female)"]
  J32 = female pin header, 4 pins [form="♀ (female)"]
  J33 = female pin header, 4 pins [form="♀ (female)"]
  J34 = female pin header, 4 pins [form="♀ (female)"]
  J35 = female pin header, 4 pins [form="♀ (female)"]
  J36 = female pin header, 4 pins [form="♀ (female)"]
  J37 = female pin header, 4 pins [form="♀ (female)"]
  J38 = female pin header, 4 pins [form="♀ (female)"]
  J39 = female pin header, 4 pins [form="♀ (female)"]
  J40 = female pin header, 4 pins [form="♀ (female)"]
  J41 = female pin header, 4 pins [form="♀ (female)"]
  J42 = female pin header, 4 pins [form="♀ (female)"]
  J43 = female pin header, 4 pins [form="♀ (female)"]
  J44 = female pin header, 4 pins [form="♀ (female)"]
  J45 = female pin header, 4 pins [form="♀ (female)"]
  J46 = female pin header, 4 pins [form="♀ (female)"]
  J47 = female pin header, 4 pins [form="♀ (female)"]
  J48 = female pin header, 4 pins [form="♀ (female)"]
  J49 = female pin header, 4 pins [form="♀ (female)"]
  J50 = female pin header, 4 pins [form="♀ (female)"]
  J51 = female pin header, 4 pins [form="♀ (female)"]
  J52 = female pin header, 4 pins [form="♀ (female)"]
  J53 = female pin header, 4 pins [form="♀ (female)"]
  J54 = female pin header, 4 pins [form="♀ (female)"]
  J55 = female pin header, 4 pins [form="♀ (female)"]
  J56 = female pin header, 4 pins [form="♀ (female)"]
  J57 = female pin header, 4 pins [form="♀ (female)"]
  J58 = female pin header, 4 pins [form="♀ (female)"]
  J59 = female pin header, 4 pins [form="♀ (female)"]
  J60 = female pin header, 4 pins [form="♀ (female)"]
  J61 = female pin header, 4 pins [form="♀ (female)"]
  J62 = female pin header, 4 pins [form="♀ (female)"]
  J63 = female pin header, 4 pins [form="♀ (female)"]
  J64 = female pin header, 4 pins [form="♀ (female)"]
  J65 = female pin header, 4 pins [form="♀ (female)"]
  J66 = female pin header, 4 pins [form="♀ (female)"]
  J67 = female pin header, 4 pins [form="♀ (female)"]
  J68 = female pin header, 4 pins [form="♀ (female)"]
  J69 = female pin header, 4 pins [form="♀ (female)"]
  J70 = female pin header, 4 pins [form="♀ (female)"]
  J71 = female pin header, 4 pins [form="♀ (female)"]
  J72 = female pin header, 4 pins [form="♀ (female)"]
  J73 = double row female pin header, 40 pins [form="♀ (female)"]
  J74 = Screw terminal - 2 pins [package=THT]
  S1 = Toggle Switch [package=THT]
  J76 = female pin header, 6 pins [form="♀ (female)"]
  J77 = female pin header, 2 pins [form="♀ (female)"]
  TRS2 = Audio Jack (TRS) 3.5mm [package="4Ucon 08780 [THT]"]
  C3 = Ceramic Capacitor [capacitance=100nF package="100 mil [THT, multilayer]"]
  C4 = Ceramic Capacitor [capacitance=100nF package="100 mil [THT, multilayer]"]
  R6 = Resistor [tolerance=±5% resistance=5k package=THT]
  R7 = Resistor [tolerance=±5% resistance=100k package=THT]
  R8 = Resistor [tolerance=±5% resistance=5k package=THT]
  R9 = Resistor [tolerance=±5% resistance=5k package=THT]
  R10 = Resistor [tolerance=±5% resistance=100k package=THT]
  J78 = female pin header, 3 pins [form="♀ (female)"]
  J79 = female pin header, 4 pins [form="♀ (female)"]
  J81 = female pin header, 4 pins [form="♀ (female)"]
  J82 = double row female pin header, 4 pins [form="♀ (female)"]
  S2 = Pushbutton [package="[THT]"]
  J75 = female pin header, 4 pins [form="♀ (female)"]
  S3 = Pushbutton [package="[THT]"]
  S4 = Pushbutton [package="[THT]"]
  S5 = Pushbutton [package="[THT]"]
  J83 = double row female pin header, 8 pins [form="♀ (female)"]

nets:
  N1: J1.pin1, J2.pin1, J3.pin1, J4.pin1, J5.pin1, J6.pin1, J7.pin1, J8.pin1, J9.pin1, J10.pin1, J11.pin1, J12.pin1, J13.pin1, J14.pin1, J15.pin1, J16.pin1, J17.pin1, J18.pin1, J19.pin1, J20.pin1, J21.pin1, J22.pin1, J23.pin1, J24.pin1, J25.pin1, J26.pin1, J27.pin1, J28.pin1, J29.pin1, J30.pin1, J31.pin1, J32.pin1, J33.pin1, J34.pin1, J35.pin1, J36.pin1, J37.pin1, J38.pin1, J39.pin1, J40.pin1, J41.pin1, J42.pin1, J43.pin1, J44.pin1, J45.pin1, J46.pin1, J47.pin1, J48.pin1, J49.pin1, J50.pin1, J51.pin1, J52.pin1, J53.pin1, J54.pin1, J55.pin1, J56.pin1, J57.pin1, J58.pin1, J59.pin1, J60.pin1, J61.pin1, J62.pin1, J63.pin1, J64.pin1, J65.pin1, J66.pin1, J67.pin1, J68.pin1, J69.pin1, J70.pin1, J71.pin1, J72.pin1, J73.pin1, S1.L1, J82.pin1
  N2: J1.pin2, J2.pin2, J3.pin2, J4.pin2, J5.pin2, J6.pin2, J7.pin2, J8.pin2, J9.pin2, J10.pin2, J11.pin2, J12.pin2, J13.pin2, J14.pin2, J15.pin2, J16.pin2, J17.pin2, J18.pin2, J19.pin2, J20.pin2, J21.pin2, J22.pin2, J23.pin2, J24.pin2, J25.pin2, J26.pin2, J27.pin2, J28.pin2, J29.pin2, J30.pin2, J31.pin2, J32.pin2, J33.pin2, J34.pin2, J35.pin2, J36.pin2, J37.pin2, J38.pin2, J39.pin2, J40.pin2, J41.pin2, J42.pin2, J43.pin2, J44.pin2, J45.pin2, J46.pin2, J47.pin2, J48.pin2, J49.pin2, J50.pin2, J51.pin2, J52.pin2, J53.pin2, J54.pin2, J55.pin2, J56.pin2, J57.pin2, J58.pin2, J59.pin2, J60.pin2, J61.pin2, J62.pin2, J63.pin2, J64.pin2, J65.pin2, J66.pin2, J67.pin2, J68.pin2, J69.pin2, J70.pin2, J71.pin2, J72.pin2, J73.pin20, J74.pin2, J82.pin2
  N3: J1.pin3, J2.pin3, J3.pin3, J4.pin3, J5.pin3, J6.pin3, J73.pin3
  N4: J1.pin4, J2.pin4, J3.pin4, J4.pin4, J5.pin4, J6.pin4, J73.pin38
  N5: J7.pin3, J8.pin3, J9.pin3, J10.pin3, J11.pin3, J12.pin3, J73.pin4
  N6: J7.pin4, J8.pin4, J9.pin4, J10.pin4, J11.pin4, J12.pin4, J73.pin37
  N7: J13.pin3, J14.pin3, J15.pin3, J16.pin3, J17.pin3, J18.pin3, J73.pin5
  N8: J13.pin4, J14.pin4, J15.pin4, J16.pin4, J17.pin4, J18.pin4, J73.pin36
  N9: J19.pin3, J20.pin3, J21.pin3, J22.pin3, J23.pin3, J24.pin3, J73.pin6
  N10: J19.pin4, J20.pin4, J21.pin4, J22.pin4, J23.pin4, J24.pin4, J73.pin35
  N11: J25.pin3, J26.pin3, J27.pin3, J28.pin3, J29.pin3, J30.pin3, J73.pin7
  N12: J25.pin4, J26.pin4, J27.pin4, J28.pin4, J29.pin4, J30.pin4, J73.pin34
  N13: J31.pin3, J32.pin3, J33.pin3, J34.pin3, J35.pin3, J36.pin3, J73.pin8
  N14: J31.pin4, J32.pin4, J33.pin4, J34.pin4, J35.pin4, J36.pin4, J73.pin33
  N15: J37.pin3, J38.pin3, J39.pin3, J40.pin3, J41.pin3, J42.pin3, J73.pin9
  N16: J37.pin4, J38.pin4, J39.pin4, J40.pin4, J41.pin4, J42.pin4, J73.pin32
  N17: J43.pin3, J44.pin3, J45.pin3, J46.pin3, J47.pin3, J48.pin3, J73.pin10
  N18: J43.pin4, J44.pin4, J45.pin4, J46.pin4, J47.pin4, J48.pin4, J73.pin31
  N19: J49.pin3, J50.pin3, J51.pin3, J52.pin3, J53.pin3, J54.pin3, J73.pin11
  N20: J49.pin4, J50.pin4, J51.pin4, J52.pin4, J53.pin4, J54.pin4, J73.pin30
  N21: J55.pin3, J56.pin3, J57.pin3, J58.pin3, J59.pin3, J60.pin3, J73.pin12
  N22: J55.pin4, J56.pin4, J57.pin4, J58.pin4, J59.pin4, J60.pin4, J73.pin29
  N23: J61.pin3, J62.pin3, J63.pin3, J64.pin3, J65.pin3, J66.pin3, J73.pin13
  N24: J61.pin4, J62.pin4, J63.pin4, J64.pin4, J65.pin4, J66.pin4, J73.pin28
  N25: J67.pin3, J68.pin3, J69.pin3, J70.pin3, J71.pin3, J72.pin3, J73.pin14
  N26: J67.pin4, J68.pin4, J69.pin4, J70.pin4, J71.pin4, J72.pin4, J73.pin27
  N27: J73.pin2, J73.pin39, J73.pin40
  N28: J73.pin19, J73.pin21, J73.pin22
  N29: J74.pin1, S1.COM, S1.L2
  N30: J76.pin1, S2.Pin_1, S2.Pin_2
  N31: J76.pin2, R6.Pin_1, J79.pin2, J81.pin2
  N32: J76.pin4, J76.pin5, J77.pin2, TRS2.Sleeve, R10.Pin_0, J78.pin1, J79.pin4, J81.pin4, J82.pin3, S2.Pin_3, S2.Pin_4, S3.Pin_3, S3.Pin_4, S4.Pin_3, S4.Pin_4, S5.Pin_3, S5.Pin_4, J83.pin1, J83.pin8
  N33: J76.pin6, J82.pin4
  N34: J77.pin1, R6.Pin_0, R7.Pin_0, J79.pin1, J81.pin1
  N35: TRS2.Ring, C3.0, J78.pin3
  N36: TRS2.Tip, C4.0, J78.pin2
  N37: C3.1, R8.Pin_0
  N38: C4.1, R9.Pin_0
  N39: R7.Pin_1, R8.Pin_1, R9.Pin_1, R10.Pin_1, J79.pin3, J81.pin3, J75.pin1
  N40: J75.pin2, S3.Pin_1, S3.Pin_2, J83.pin2, J83.pin7
  N41: J75.pin3, S4.Pin_1, S4.Pin_2, J83.pin3, J83.pin6
  N42: J75.pin4, S5.Pin_1, S5.Pin_2, J83.pin4, J83.pin5

notes:
  +
  -
  SegTerm
  AREF
  GND
  RESET
  3.3V
  5V
  Vin
  A0
  A1
  by KreativeKorp
  L
  R
  LED+
  LED-
  ArVin
  ArGND
  Ar5V
  A2
  A3
  < cut to disconnect audio jack
  cut to disconnect buttons >
