# Fritzing sketch TacText (saved by Fritzing 0.9.2b)
circuit board: 16.4cm x 6.2cm
breadboards: 1

parts:
  esc = Pushbutton [package="[THT]"]
  1_! = Pushbutton [package="[THT]"]
  2_@ = Pushbutton [package="[THT]"]
  3_# = Pushbutton [package="[THT]"]
  4_$ = Pushbutton [package="[THT]"]
  5_% = Pushbutton [package="[THT]"]
  6_^ = Pushbutton [package="[THT]"]
  7_& = Pushbutton [package="[THT]"]
  8_* = Pushbutton [package="[THT]"]
  9_( = Pushbutton [package="[THT]"]
  0_) = Pushbutton [package="[THT]"]
  - = Pushbutton [package="[THT]"]
  =_+ = Pushbutton [package="[THT]"]
  bksp = Pushbutton [package="[THT]"]
  del = Pushbutton [package="[THT]"]
  E_e = Pushbutton [package="[THT]"]
  W_w = Pushbutton [package="[THT]"]
  tab = Pushbutton [package="[THT]"]
  P_p = Pushbutton [package="[THT]"]
  T_t = Pushbutton [package="[THT]"]
  \_| = Pushbutton [package="[THT]"]
  [_{ = Pushbutton [package="[THT]"]
  Y_y = Pushbutton [package="[THT]"]
  ]_} = Pushbutton [package="[THT]"]
  I_i = Pushbutton [package="[THT]"]
  O_o = Pushbutton [package="[THT]"]
  U_u = Pushbutton [package="[THT]"]
  `_~ = Pushbutton [package="[THT]"]
  R_r = Pushbutton [package="[THT]"]
  Q_q = Pushbutton [package="[THT]"]
  <-- = Pushbutton [package="[THT]"]
  > = Pushbutton [package="[THT]"]
  S_s = Pushbutton [package="[THT]"]
  A_a = Pushbutton [package="[THT]"]
  shift = Pushbutton [package="[THT]"]
  caps = Pushbutton [package="[THT]"]
  <_> = Pushbutton [package="[THT]"]
  N_n = Pushbutton [package="[THT]"]
  C_c = Pushbutton [package="[THT]"]
  shift_2 = Pushbutton [package="[THT]"]
  V_v = Pushbutton [package="[THT]"]
  X_x = Pushbutton [package="[THT]"]
  ; = Pushbutton [package="[THT]"]
  B_b = Pushbutton [package="[THT]"]
  /_? = Pushbutton [package="[THT]"]
  G_g = Pushbutton [package="[THT]"]
  rtn = Pushbutton [package="[THT]"]
  '_" = Pushbutton [package="[THT]"]
  F_f = Pushbutton [package="[THT]"]
  K_k = Pushbutton [package="[THT]"]
  Z_z = Pushbutton [package="[THT]"]
  --> = Pushbutton [package="[THT]"]
  /|\ = Pushbutton [package="[THT]"]
  J_j = Pushbutton [package="[THT]"]
  L_l = Pushbutton [package="[THT]"]
  < = Pushbutton [package="[THT]"]
  D_d = Pushbutton [package="[THT]"]
  H_h = Pushbutton [package="[THT]"]
  M_m = Pushbutton [package="[THT]"]
  alt = Pushbutton [package="[THT]"]
  ctrl = Pushbutton [package="[THT]"]
  alt_2 = Pushbutton [package="[THT]"]
  spc = Pushbutton [package="[THT]"]
  ctrl_2 = Pushbutton [package="[THT]"]
  spc_2 = Pushbutton [package="[THT]"]
  \|/ = Pushbutton [package="[THT]"]
  spc_3 = Pushbutton [package="[THT]"]
  LED1 = LED - 5mm [color="Red (633nm)" package="5 mm [THT]"]
  U1 = DIODE-ZENER [package=diode-zener]
  U2 = DIODE-ZENER [package=diode-zener]
  U3 = DIODE-ZENER [package=diode-zener]
  U4 = DIODE-ZENER [package=diode-zener]
  U5 = DIODE-ZENER [package=diode-zener]
  U6 = DIODE-ZENER [package=diode-zener]
  U7 = DIODE-ZENER [package=diode-zener]
  U8 = DIODE-ZENER [package=diode-zener]
  U9 = DIODE-ZENER [package=diode-zener]
  U10 = DIODE-ZENER [package=diode-zener]
  U11 = DIODE-ZENER [package=diode-zener]
  U12 = DIODE-ZENER [package=diode-zener]
  U13 = DIODE-ZENER [package=diode-zener]
  U14 = DIODE-ZENER [package=diode-zener]
  U15 = DIODE-ZENER [package=diode-zener]
  U16 = DIODE-ZENER [package=diode-zener]
  U17 = DIODE-ZENER [package=diode-zener]
  U18 = DIODE-ZENER [package=diode-zener]
  U19 = DIODE-ZENER [package=diode-zener]
  U20 = DIODE-ZENER [package=diode-zener]
  U21 = DIODE-ZENER [package=diode-zener]
  U22 = DIODE-ZENER [package=diode-zener]
  U23 = DIODE-ZENER [package=diode-zener]
  U24 = DIODE-ZENER [package=diode-zener]
  U25 = DIODE-ZENER [package=diode-zener]
  U26 = DIODE-ZENER [package=diode-zener]
  U27 = DIODE-ZENER [package=diode-zener]
  U28 = DIODE-ZENER [package=diode-zener]
  U29 = DIODE-ZENER [package=diode-zener]
  U30 = DIODE-ZENER [package=diode-zener]
  U31 = DIODE-ZENER [package=diode-zener]
  U32 = DIODE-ZENER [package=diode-zener]
  U33 = DIODE-ZENER [package=diode-zener]
  U34 = DIODE-ZENER [package=diode-zener]
  U35 = DIODE-ZENER [package=diode-zener]
  U37 = DIODE-ZENER [package=diode-zener]
  U38 = DIODE-ZENER [package=diode-zener]
  U39 = DIODE-ZENER [package=diode-zener]
  U40 = DIODE-ZENER [package=diode-zener]
  U41 = DIODE-ZENER [package=diode-zener]
  U42 = DIODE-ZENER [package=diode-zener]
  U43 = DIODE-ZENER [package=diode-zener]
  U44 = DIODE-ZENER [package=diode-zener]
  U45 = DIODE-ZENER [package=diode-zener]
  U46 = DIODE-ZENER [package=diode-zener]
  U47 = DIODE-ZENER [package=diode-zener]
  U48 = DIODE-ZENER [package=diode-zener]
  U49 = DIODE-ZENER [package=diode-zener]
  U50 = DIODE-ZENER [package=diode-zener]
  U52 = DIODE-ZENER [package=diode-zener]
  U53 = DIODE-ZENER [package=diode-zener]
  U54 = DIODE-ZENER [package=diode-zener]
  U55 = DIODE-ZENER [package=diode-zener]
  U56 = DIODE-ZENER [package=diode-zener]
  U57 = DIODE-ZENER [package=diode-zener]
  U58 = DIODE-ZENER [package=diode-zener]
  U59 = DIODE-ZENER [package=diode-zener]
  U60 = DIODE-ZENER [package=diode-zener]
  U63 = DIODE-ZENER [package=diode-zener]
  U66 = DIODE-ZENER [package=diode-zener]
  U69 = DIODE-ZENER [package=diode-zener]
  U71 = DIODE-ZENER [package=diode-zener]
  U73 = DIODE-ZENER [package=diode-zener]
  U75 = DIODE-ZENER [package=diode-zener]
  J1 = female pin header, 18 pins [form="♀ (female)"]
  R1 = Resistor [tolerance=±5% resistance=220 package=THT]

nets:
  N1: esc.Pin_1, esc.Pin_2, 1_!.Pin_1, 1_!.Pin_2, 2_@.Pin_1, 2_@.Pin_2, 3_#.Pin_1, 3_#.Pin_2, 4_$.Pin_1, 4_$.Pin_2, 5_%.Pin_1, 5_%.Pin_2, 6_^.Pin_1, 6_^.Pin_2, ctrl.Pin_1, ctrl.Pin_2, J1.pin3
  N2: esc.Pin_3, U1.A
  N3: 1_!.Pin_3, U2.A
  N4: 2_@.Pin_3, U3.A
  N5: 3_#.Pin_3, U4.A
  N6: 4_$.Pin_3, U5.A
  N7: 5_%.Pin_3, U10.A
  N8: 6_^.Pin_3, 6_^.Pin_4, U6.A
  N9: 7_&.Pin_1, 8_*.Pin_1, 8_*.Pin_2, 9_(.Pin_1, 9_(.Pin_2, 0_).Pin_1, 0_).Pin_2, -.Pin_1, -.Pin_2, =_+.Pin_1, =_+.Pin_2, bksp.Pin_1, bksp.Pin_2, del.Pin_2, J1.pin10
  N10: 7_&.Pin_3, 7_&.Pin_4, U8.A
  N11: 8_*.Pin_3, 8_*.Pin_4, U7.A
  N12: 9_(.Pin_3, 9_(.Pin_4, U9.A
  N13: 0_).Pin_3, U11.A
  N14: -.Pin_3, -.Pin_4, U15.A
  N15: =_+.Pin_3, =_+.Pin_4, U14.A
  N16: bksp.Pin_3, bksp.Pin_4, U12.A
  N17: del.Pin_3, del.Pin_4, U13.A
  N18: E_e.Pin_1, E_e.Pin_2, W_w.Pin_1, W_w.Pin_2, tab.Pin_1, tab.Pin_2, T_t.Pin_1, T_t.Pin_2, Y_y.Pin_1, Y_y.Pin_2, R_r.Pin_1, R_r.Pin_2, Q_q.Pin_1, Q_q.Pin_2, alt.Pin_2, J1.pin4
  N19: E_e.Pin_3, U28.A
  N20: W_w.Pin_3, U16.A
  N21: tab.Pin_3, U24.A
  N22: P_p.Pin_1, P_p.Pin_2, \_|.Pin_1, \_|.Pin_2, [_{.Pin_1, [_{.Pin_2, ]_}.Pin_1, ]_}.Pin_2, I_i.Pin_1, I_i.Pin_2, O_o.Pin_1, O_o.Pin_2, U_u.Pin_1, `_~.Pin_2, J1.pin9
  N23: P_p.Pin_3, U20.A
  N24: T_t.Pin_3, U17.A
  N25: \_|.Pin_3, \_|.Pin_4, U21.A
  N26: [_{.Pin_3, [_{.Pin_4, U27.A
  N27: Y_y.Pin_3, Y_y.Pin_4, U19.A
  N28: ]_}.Pin_3, ]_}.Pin_4, U22.A
  N29: I_i.Pin_3, I_i.Pin_4, U29.A
  N30: O_o.Pin_3, O_o.Pin_4, U18.A
  N31: U_u.Pin_3, U_u.Pin_4, U23.A
  N32: `_~.Pin_3, `_~.Pin_4, U26.A
  N33: R_r.Pin_3, U30.A
  N34: Q_q.Pin_3, U25.A
  N35: <--.Pin_1, <--.Pin_2, >.Pin_1, >.Pin_2, shift.Pin_1, shift.Pin_2, shift_2.Pin_1, shift_2.Pin_2, /_?.Pin_1, /_?.Pin_2, -->.Pin_2, <.Pin_1, <.Pin_2, M_m.Pin_1, M_m.Pin_2, ctrl_2.Pin_1, ctrl_2.Pin_2, J1.pin7
  N36: <--.Pin_3, <--.Pin_4, U57.A
  N37: >.Pin_3, U48.A
  N38: S_s.Pin_1, S_s.Pin_2, A_a.Pin_1, A_a.Pin_2, caps.Pin_1, caps.Pin_2, G_g.Pin_1, G_g.Pin_2, F_f.Pin_1, F_f.Pin_2, D_d.Pin_1, D_d.Pin_2, H_h.Pin_1, H_h.Pin_2, spc.Pin_1, spc.Pin_2, spc_2.Pin_2, spc_3.Pin_1, J1.pin5
  N39: S_s.Pin_3, S_s.Pin_4, U41.A
  N40: A_a.Pin_3, A_a.Pin_4, U43.A
  N41: shift.Pin_3, shift.Pin_4, shift_2.Pin_3, shift_2.Pin_4, U49.A
  N42: caps.Pin_3, caps.Pin_4, U40.A
  N43: <_>.Pin_1, <_>.Pin_2, N_n.Pin_2, C_c.Pin_1, C_c.Pin_2, V_v.Pin_1, V_v.Pin_2, X_x.Pin_1, X_x.Pin_2, B_b.Pin_1, B_b.Pin_2, Z_z.Pin_1, Z_z.Pin_2, alt_2.Pin_1, alt_2.Pin_2, J1.pin6
  N44: <_>.Pin_3, U54.A
  N45: N_n.Pin_3, N_n.Pin_4, U59.A
  N46: C_c.Pin_3, U50.A
  N47: V_v.Pin_3, U53.A
  N48: X_x.Pin_3, U46.A
  N49: ;.Pin_1, ;.Pin_2, rtn.Pin_1, rtn.Pin_2, '_".Pin_1, '_".Pin_2, K_k.Pin_1, K_k.Pin_2, /|\.Pin_2, J_j.Pin_1, J_j.Pin_2, L_l.Pin_1, L_l.Pin_2, \|/.Pin_1, J1.pin8
  N50: ;.Pin_3, ;.Pin_4, U45.A
  N51: B_b.Pin_3, B_b.Pin_4, U47.A
  N52: /_?.Pin_3, /_?.Pin_4, U60.A
  N53: G_g.Pin_3, G_g.Pin_4, U35.A
  N54: rtn.Pin_3, rtn.Pin_4, U44.A
  N55: '_".Pin_3, '_".Pin_4, U39.A
  N56: F_f.Pin_3, U38.A
  N57: K_k.Pin_3, K_k.Pin_4, U31.A
  N58: Z_z.Pin_3, U52.A
  N59: -->.Pin_3, -->.Pin_4, U56.A
  N60: /|\.Pin_3, /|\.Pin_4, U37.A
  N61: J_j.Pin_3, J_j.Pin_4, U32.A
  N62: L_l.Pin_3, U33.A
  N63: <.Pin_3, <.Pin_4, U55.A
  N64: D_d.Pin_3, D_d.Pin_4, U42.A
  N65: H_h.Pin_3, H_h.Pin_4, U34.A
  N66: M_m.Pin_3, M_m.Pin_4, U58.A
  N67: alt.Pin_3, U73.A
  N68: ctrl.Pin_3, U63.A
  N69: alt_2.Pin_3, U71.A
  N70: spc.Pin_3, spc.Pin_4, spc_2.Pin_4, spc_3.Pin_3, U75.A
  N71: ctrl_2.Pin_3, ctrl_2.Pin_4, U66.A
  N72: \|/.Pin_3, \|/.Pin_4, U69.A
  N73: LED1.cathode, J1.pin1
  N74: LED1.anode, R1.Pin_0
  N75: U1.C, U12.C, U21.C, U24.C, U37.C, U40.C, U54.C, U56.C, J1.pin17
  N76: U2.C, U14.C, U22.C, U25.C, U43.C, U44.C, U52.C, U57.C, J1.pin16
  N77: U3.C, U15.C, U16.C, U27.C, U39.C, U41.C, U46.C, U49.C, J1.pin15
  N78: U4.C, U11.C, U20.C, U28.C, U42.C, U45.C, U50.C, U60.C, J1.pin14
  N79: U5.C, U9.C, U18.C, U30.C, U33.C, U38.C, U48.C, U53.C, J1.pin13
  N80: U6.C, U8.C, U19.C, U23.C, U32.C, U34.C, U58.C, U59.C, J1.pin11
  N81: U7.C, U10.C, U17.C, U29.C, U31.C, U35.C, U47.C, U55.C, J1.pin12
  N82: U13.C, U26.C, U63.C, U66.C, U69.C, U71.C, U73.C, U75.C, J1.pin18
  N83: J1.pin2, R1.Pin_1

notes:
  TacText by KreativeKorp
  |--Cols/Caths--|
  |---Rows/Ans---|
  LEDA
  LEDC
  1
  18
  3
  11
  10
  2
