# Fritzing sketch TacTune (saved by Fritzing 0.9.2b)
circuit board: 39.3cm x 3.4cm
breadboards: 1

parts:
  A = Pushbutton [package="[THT]"]
  U14 = DIODE-ZENER [package=diode-zener]
  A# = Pushbutton [package="[THT]"]
  U15 = DIODE-ZENER [package=diode-zener]
  B = Pushbutton [package="[THT]"]
  U16 = DIODE-ZENER [package=diode-zener]
  C = Pushbutton [package="[THT]"]
  U17 = DIODE-ZENER [package=diode-zener]
  C# = Pushbutton [package="[THT]"]
  U18 = DIODE-ZENER [package=diode-zener]
  D = Pushbutton [package="[THT]"]
  U19 = DIODE-ZENER [package=diode-zener]
  D# = Pushbutton [package="[THT]"]
  U20 = DIODE-ZENER [package=diode-zener]
  E = Pushbutton [package="[THT]"]
  U21 = DIODE-ZENER [package=diode-zener]
  F = Pushbutton [package="[THT]"]
  U22 = DIODE-ZENER [package=diode-zener]
  F# = Pushbutton [package="[THT]"]
  U23 = DIODE-ZENER [package=diode-zener]
  G = Pushbutton [package="[THT]"]
  U24 = DIODE-ZENER [package=diode-zener]
  G# = Pushbutton [package="[THT]"]
  U25 = DIODE-ZENER [package=diode-zener]
  A_2 = Pushbutton [package="[THT]"]
  U26 = DIODE-ZENER [package=diode-zener]
  A#_2 = Pushbutton [package="[THT]"]
  U27 = DIODE-ZENER [package=diode-zener]
  B_2 = Pushbutton [package="[THT]"]
  U28 = DIODE-ZENER [package=diode-zener]
  C_2 = Pushbutton [package="[THT]"]
  U29 = DIODE-ZENER [package=diode-zener]
  F_2 = Pushbutton [package="[THT]"]
  A_3 = Pushbutton [package="[THT]"]
  C#_2 = Pushbutton [package="[THT]"]
  C_3 = Pushbutton [package="[THT]"]
  D_2 = Pushbutton [package="[THT]"]
  D#_2 = Pushbutton [package="[THT]"]
  A#_3 = Pushbutton [package="[THT]"]
  G_2 = Pushbutton [package="[THT]"]
  B_3 = Pushbutton [package="[THT]"]
  E_2 = Pushbutton [package="[THT]"]
  G#_2 = Pushbutton [package="[THT]"]
  F#_2 = Pushbutton [package="[THT]"]
  U30 = DIODE-ZENER [package=diode-zener]
  U31 = DIODE-ZENER [package=diode-zener]
  U32 = DIODE-ZENER [package=diode-zener]
  U33 = DIODE-ZENER [package=diode-zener]
  U34 = DIODE-ZENER [package=diode-zener]
  U35 = DIODE-ZENER [package=diode-zener]
  U36 = DIODE-ZENER [package=diode-zener]
  U37 = DIODE-ZENER [package=diode-zener]
  U38 = DIODE-ZENER [package=diode-zener]
  U39 = DIODE-ZENER [package=diode-zener]
  U40 = DIODE-ZENER [package=diode-zener]
  U41 = DIODE-ZENER [package=diode-zener]
  G_3 = Pushbutton [package="[THT]"]
  C_4 = Pushbutton [package="[THT]"]
  B_4 = Pushbutton [package="[THT]"]
  F_3 = Pushbutton [package="[THT]"]
  C#_3 = Pushbutton [package="[THT]"]
  A#_4 = Pushbutton [package="[THT]"]
  E_3 = Pushbutton [package="[THT]"]
  G#_3 = Pushbutton [package="[THT]"]
  D#_3 = Pushbutton [package="[THT]"]
  A_4 = Pushbutton [package="[THT]"]
  F#_3 = Pushbutton [package="[THT]"]
  D_3 = Pushbutton [package="[THT]"]
  U42 = DIODE-ZENER [package=diode-zener]
  U43 = DIODE-ZENER [package=diode-zener]
  U44 = DIODE-ZENER [package=diode-zener]
  U45 = DIODE-ZENER [package=diode-zener]
  U46 = DIODE-ZENER [package=diode-zener]
  U47 = DIODE-ZENER [package=diode-zener]
  U48 = DIODE-ZENER [package=diode-zener]
  U49 = DIODE-ZENER [package=diode-zener]
  U50 = DIODE-ZENER [package=diode-zener]
  U51 = DIODE-ZENER [package=diode-zener]
  U52 = DIODE-ZENER [package=diode-zener]
  U53 = DIODE-ZENER [package=diode-zener]
  C#_4 = Pushbutton [package="[THT]"]
  A_5 = Pushbutton [package="[THT]"]
  E_4 = Pushbutton [package="[THT]"]
  D_4 = Pushbutton [package="[THT]"]
  C_5 = Pushbutton [package="[THT]"]
  F_4 = Pushbutton [package="[THT]"]
  G#_4 = Pushbutton [package="[THT]"]
  D#_4 = Pushbutton [package="[THT]"]
  F#_4 = Pushbutton [package="[THT]"]
  A#_5 = Pushbutton [package="[THT]"]
  G_4 = Pushbutton [package="[THT]"]
  B_5 = Pushbutton [package="[THT]"]
  U54 = DIODE-ZENER [package=diode-zener]
  U55 = DIODE-ZENER [package=diode-zener]
  U56 = DIODE-ZENER [package=diode-zener]
  U57 = DIODE-ZENER [package=diode-zener]
  U58 = DIODE-ZENER [package=diode-zener]
  U59 = DIODE-ZENER [package=diode-zener]
  U60 = DIODE-ZENER [package=diode-zener]
  U61 = DIODE-ZENER [package=diode-zener]
  U62 = DIODE-ZENER [package=diode-zener]
  U63 = DIODE-ZENER [package=diode-zener]
  U64 = DIODE-ZENER [package=diode-zener]
  U65 = DIODE-ZENER [package=diode-zener]
  D#_5 = Pushbutton [package="[THT]"]
  G_5 = Pushbutton [package="[THT]"]
  C_6 = Pushbutton [package="[THT]"]
  E_5 = Pushbutton [package="[THT]"]
  G#_5 = Pushbutton [package="[THT]"]
  F#_5 = Pushbutton [package="[THT]"]
  A#_6 = Pushbutton [package="[THT]"]
  B_6 = Pushbutton [package="[THT]"]
  F_5 = Pushbutton [package="[THT]"]
  C#_5 = Pushbutton [package="[THT]"]
  A_6 = Pushbutton [package="[THT]"]
  D_5 = Pushbutton [package="[THT]"]
  U66 = DIODE-ZENER [package=diode-zener]
  U67 = DIODE-ZENER [package=diode-zener]
  U68 = DIODE-ZENER [package=diode-zener]
  U69 = DIODE-ZENER [package=diode-zener]
  U70 = DIODE-ZENER [package=diode-zener]
  U71 = DIODE-ZENER [package=diode-zener]
  U72 = DIODE-ZENER [package=diode-zener]
  U73 = DIODE-ZENER [package=diode-zener]
  U74 = DIODE-ZENER [package=diode-zener]
  U75 = DIODE-ZENER [package=diode-zener]
  U76 = DIODE-ZENER [package=diode-zener]
  U77 = DIODE-ZENER [package=diode-zener]
  J2 = female pin header, 18 pins [form="♀ (female)"]
  LED1 = LED - 5mm [color="Red (633nm)" package="5 mm [THT]"]
  R1 = Resistor [tolerance=±5% resistance=220 package=THT]

nets:
  N1: A.Pin_1, A#.Pin_1, B.Pin_1, B.Pin_2, C.Pin_1, C.Pin_2, C#.Pin_1, C#.Pin_2, D.Pin_1, D.Pin_2, D#.Pin_2, E.Pin_2, J2.pin3
  N2: A.Pin_3, A.Pin_4, U14.A
  N3: U14.C, U22.C, U31.C, U41.C, U45.C, U55.C, U59.C, U76.C, J2.pin11
  N4: A#.Pin_3, A#.Pin_4, U15.A
  N5: U15.C, U23.C, U32.C, U35.C, U49.C, U57.C, U64.C, U70.C, J2.pin12
  N6: B.Pin_3, B.Pin_4, U16.A
  N7: U16.C, U24.C, U34.C, U40.C, U44.C, U54.C, U56.C, U73.C, J2.pin13
  N8: C.Pin_3, C.Pin_4, U17.A
  N9: U17.C, U25.C, U36.C, U39.C, U47.C, U63.C, U65.C, U75.C, J2.pin14
  N10: C#.Pin_3, C#.Pin_4, U18.A
  N11: U18.C, U26.C, U38.C, U42.C, U48.C, U58.C, U69.C, U77.C, J2.pin15
  N12: D.Pin_3, D.Pin_4, U19.A
  N13: U19.C, U27.C, U37.C, U46.C, U53.C, U61.C, U71.C, U74.C, J2.pin16
  N14: D#.Pin_3, D#.Pin_4, U20.A
  N15: U20.C, U28.C, U33.C, U51.C, U52.C, U60.C, U67.C, U72.C, J2.pin17
  N16: E.Pin_3, E.Pin_4, U21.A
  N17: U21.C, U29.C, U30.C, U43.C, U50.C, U62.C, U66.C, U68.C, J2.pin18
  N18: F.Pin_1, F.Pin_2, F#.Pin_1, F#.Pin_2, G.Pin_1, G.Pin_2, G#.Pin_1, G#.Pin_2, A_2.Pin_1, A_2.Pin_2, A#_2.Pin_2, B_2.Pin_1, B_2.Pin_2, C_2.Pin_2, J2.pin4
  N19: F.Pin_3, F.Pin_4, U22.A
  N20: F#.Pin_3, F#.Pin_4, U23.A
  N21: G.Pin_3, G.Pin_4, U24.A
  N22: G#.Pin_3, G#.Pin_4, U25.A
  N23: A_2.Pin_3, A_2.Pin_4, U26.A
  N24: A#_2.Pin_3, A#_2.Pin_4, U27.A
  N25: B_2.Pin_3, B_2.Pin_4, U28.A
  N26: C_2.Pin_3, C_2.Pin_4, U29.A
  N27: F_2.Pin_1, F_2.Pin_2, C#_2.Pin_1, D_2.Pin_1, D#_2.Pin_1, D#_2.Pin_2, G_2.Pin_2, E_2.Pin_1, E_2.Pin_2, G#_2.Pin_2, F#_2.Pin_1, F#_2.Pin_2, J2.pin5
  N28: F_2.Pin_3, F_2.Pin_4, U38.A
  N29: A_3.Pin_1, C_3.Pin_1, C_3.Pin_2, A#_3.Pin_1, B_3.Pin_1, B_3.Pin_2, C#_3.Pin_1, C#_3.Pin_2, E_3.Pin_2, D#_3.Pin_2, D_3.Pin_1, D_3.Pin_2, J2.pin6
  N30: A_3.Pin_3, A_3.Pin_4, U41.A
  N31: C#_2.Pin_3, C#_2.Pin_4, U31.A
  N32: C_3.Pin_3, C_3.Pin_4, U39.A
  N33: D_2.Pin_3, D_2.Pin_4, U32.A
  N34: D#_2.Pin_3, D#_2.Pin_4, U34.A
  N35: A#_3.Pin_3, A#_3.Pin_4, U35.A
  N36: G_2.Pin_3, G_2.Pin_4, U33.A
  N37: B_3.Pin_3, B_3.Pin_4, U40.A
  N38: E_2.Pin_3, E_2.Pin_4, U36.A
  N39: G#_2.Pin_3, G#_2.Pin_4, U30.A
  N40: F#_2.Pin_3, F#_2.Pin_4, U37.A
  N41: G_3.Pin_1, G_3.Pin_2, C_4.Pin_2, B_4.Pin_1, B_4.Pin_2, F_3.Pin_1, F_3.Pin_2, A#_4.Pin_2, G#_3.Pin_1, G#_3.Pin_2, A_4.Pin_1, A_4.Pin_2, F#_3.Pin_1, F#_3.Pin_2, J2.pin7
  N42: G_3.Pin_3, G_3.Pin_4, U44.A
  N43: C_4.Pin_3, C_4.Pin_4, U50.A
  N44: B_4.Pin_3, B_4.Pin_4, U52.A
  N45: F_3.Pin_3, F_3.Pin_4, U45.A
  N46: C#_3.Pin_3, C#_3.Pin_4, U42.A
  N47: A#_4.Pin_3, A#_4.Pin_4, U46.A
  N48: E_3.Pin_3, E_3.Pin_4, U43.A
  N49: G#_3.Pin_3, G#_3.Pin_4, U47.A
  N50: D#_3.Pin_3, D#_3.Pin_4, U51.A
  N51: A_4.Pin_3, A_4.Pin_4, U48.A
  N52: F#_3.Pin_3, F#_3.Pin_4, U49.A
  N53: D_3.Pin_3, D_3.Pin_4, U53.A
  N54: C#_4.Pin_1, E_4.Pin_1, E_4.Pin_2, D_4.Pin_1, F_4.Pin_1, F_4.Pin_2, G#_4.Pin_2, D#_4.Pin_1, D#_4.Pin_2, F#_4.Pin_1, F#_4.Pin_2, G_4.Pin_2, J2.pin8
  N55: C#_4.Pin_3, C#_4.Pin_4, U55.A
  N56: A_5.Pin_1, C_5.Pin_1, C_5.Pin_2, A#_5.Pin_1, B_5.Pin_1, B_5.Pin_2, D#_5.Pin_2, E_5.Pin_2, C#_5.Pin_1, C#_5.Pin_2, D_5.Pin_1, D_5.Pin_2, J2.pin9
  N57: A_5.Pin_3, A_5.Pin_4, U59.A
  N58: E_4.Pin_3, E_4.Pin_4, U63.A
  N59: D_4.Pin_3, D_4.Pin_4, U57.A
  N60: C_5.Pin_3, C_5.Pin_4, U65.A
  N61: F_4.Pin_3, F_4.Pin_4, U58.A
  N62: G#_4.Pin_3, G#_4.Pin_4, U62.A
  N63: D#_4.Pin_3, D#_4.Pin_4, U56.A
  N64: F#_4.Pin_3, F#_4.Pin_4, U61.A
  N65: A#_5.Pin_3, A#_5.Pin_4, U64.A
  N66: G_4.Pin_3, G_4.Pin_4, U60.A
  N67: B_5.Pin_3, B_5.Pin_4, U54.A
  N68: D#_5.Pin_3, D#_5.Pin_4, U72.A
  N69: G_5.Pin_1, G_5.Pin_2, C_6.Pin_2, G#_5.Pin_1, G#_5.Pin_2, F#_5.Pin_1, F#_5.Pin_2, A#_6.Pin_2, B_6.Pin_1, B_6.Pin_2, F_5.Pin_1, F_5.Pin_2, A_6.Pin_1, A_6.Pin_2, J2.pin10
  N70: G_5.Pin_3, G_5.Pin_4, U73.A
  N71: C_6.Pin_3, C_6.Pin_4, U66.A
  N72: E_5.Pin_3, E_5.Pin_4, U68.A
  N73: G#_5.Pin_3, G#_5.Pin_4, U75.A
  N74: F#_5.Pin_3, F#_5.Pin_4, U70.A
  N75: A#_6.Pin_3, A#_6.Pin_4, U74.A
  N76: B_6.Pin_3, B_6.Pin_4, U67.A
  N77: F_5.Pin_3, F_5.Pin_4, U76.A
  N78: C#_5.Pin_3, C#_5.Pin_4, U77.A
  N79: A_6.Pin_3, A_6.Pin_4, U69.A
  N80: D_5.Pin_3, D_5.Pin_4, U71.A
  N81: J2.pin1, LED1.cathode
  N82: J2.pin2, R1.Pin_0
  N83: LED1.anode, R1.Pin_1

notes:
  2
  10
  11
  3
  18
  1
  LEDC
  LEDA
  |---Rows/Ans---|
  |--Cols/Caths--|
  MIDC
  A440
  TacTune by KreativeKorp
